# Fritzing sketch espxmas (saved by Fritzing 0.9.3b)
breadboards: 1

parts:
  WeMos_D1_Mini1 = WeMos D1 Mini
  R1 = Resistor [tolerance=±5% resistance=1k package=THT]
  LED1 = LED - 5mm [color="Green (560nm)" package="5 mm [THT]"]
  S1 = Pushbutton [package="[THT]"]
  R4 = Resistor [tolerance=±5% resistance=10k package="0805 [SMD]"]
  R3 = Rotary Potentiometer (Small) [maximum_resistance=10kΩ package=THT]

nets:
  N1: WeMos_D1_Mini1.3V3, S1.Pin_1, S1.Pin_2, R3.leg2
  N2: WeMos_D1_Mini1.A0, R3.wiper
  N3: WeMos_D1_Mini1.D0, S1.Pin_3, S1.Pin_4, R4.Pin_0
  N4: WeMos_D1_Mini1.D1, R1.Pin_0
  N5: WeMos_D1_Mini1.G, LED1.cathode, R4.Pin_1, R3.leg1
  N6: R1.Pin_1, LED1.anode
